# Fritzing sketch Untitled Sketch (saved by Fritzing 0.8.7b)
breadboards: 1

parts:
  부품1 = Arduino Uno (Rev3)
  M1 = DC Motor
  S1 = H-Bridge with L298N
  M2 = DC Motor

nets:
  N1: 부품1.D2, S1.IN3
  N2: 부품1.D3_PWM, S1.IN4
  N3: 부품1.D4, S1.IN2
  N4: 부품1.D5_PWM, S1.IN1
  5V: 부품1.5V, S1.5V
  GND: 부품1.GND, S1.GND
  VIN: 부품1.VIN, S1.12V
  N5: M1.pin_1, S1.M2-02
  N6: M1.pin_2, S1.M2-01
  N7: S1.M1-01, M2.pin_2
  N8: S1.M1-02, M2.pin_1

custom parts:
  H-Bridge with L298N: h-bridge
